// Logisim project final_transfer.circ as structural Verilog: 1 circuit, main circuit main
module main (
  input  in_1
);

  wire clock_1_out;
  wire [2:0] Counter_q;
  wire [14:0] rom_1_data;
  wire [27:0] controlled_buffer_1_out, Reg_A_q, Reg_B_q, Reg_C_q, Reg_D_q, Reg_E_q;

  Clock clock_1 (.out(clock_1_out));
  Counter #(.width(3), .max('h4)) Counter (
    .count(1'b1), .Q(Counter_q), .clk(clock_1_out), .clr(in_1));  // open: load, D, carry
  ROM #(.addrWidth(3), .dataWidth(15)) rom_1 (.addr(Counter_q), .data(rom_1_data));  // open: sel
  Register #(.width(28)) Reg_A (
    .D(controlled_buffer_1_out), .en(rom_1_data[5]), .Q(Reg_A_q), .clk(clock_1_out), .clr(rom_1_data[10]));
  Register #(.width(28)) Reg_B (
    .D(controlled_buffer_1_out), .en(rom_1_data[6]), .Q(Reg_B_q), .clk(clock_1_out), .clr(rom_1_data[11]));
  Register #(.width(28)) Reg_C (
    .D(controlled_buffer_1_out), .en(rom_1_data[7]), .Q(Reg_C_q), .clk(clock_1_out), .clr(rom_1_data[12]));
  Register #(.width(28)) Reg_D (
    .D(controlled_buffer_1_out), .en(rom_1_data[8]), .Q(Reg_D_q), .clk(clock_1_out), .clr(rom_1_data[13]));
  Register #(.width(28)) Reg_E (
    .D(controlled_buffer_1_out), .en(rom_1_data[9]), .Q(Reg_E_q), .clk(clock_1_out), .clr(rom_1_data[14]));
  assign controlled_buffer_1_out = rom_1_data[0] ? Reg_A_q : 28'bz;  // Controlled_Buffer controlled_buffer_1
  assign controlled_buffer_1_out = rom_1_data[1] ? Reg_B_q : 28'bz;  // Controlled_Buffer controlled_buffer_2
  assign controlled_buffer_1_out = rom_1_data[2] ? Reg_C_q : 28'bz;  // Controlled_Buffer controlled_buffer_3
  assign controlled_buffer_1_out = rom_1_data[3] ? Reg_D_q : 28'bz;  // Controlled_Buffer controlled_buffer_4
  assign controlled_buffer_1_out = rom_1_data[4] ? Reg_E_q : 28'bz;  // Controlled_Buffer controlled_buffer_5

  // Notes on the sheet:
  //   contents of rom_1 (hex, n*v repeats v):
  //   4048 2082 904 1208 110
endmodule
